# Fritzing sketch raspi3_qr-scanner (saved by Fritzing 0.9.5d)

parts:
  Raspberry_Pi_1 = Raspberry Pi 3 [part_number=RPI-3-V1.2]
  Grove2 = Grove OLED 128x96

nets:
  3V3: Raspberry_Pi_1.3v3, Grove2.VCC
  N1: Raspberry_Pi_1.GPIO2, Grove2.SDA
  N2: Raspberry_Pi_1.GPIO3, Grove2.SCL
  GND: Raspberry_Pi_1.GND, Grove2.GND
